# Fritzing sketch Poubelle (saved by Fritzing 0.9.3b)

parts:
  Composant1 = Adafruit 2.8inch Resistive TFT [part_number="Adafruit #1770"]
  Composant2 = Arduino Uno (Rev3)
  WeMos_D1_R1 = WeMos D1 R2  # not connected
  PIR1 = PIR sensor
  Composant3 = Adafruit PN532 NFC RFID Controller Shield [part_number="Adafruit #789"]  # not connected

nets:
  N1: Composant1.LCD_CD_SCK, Composant2.D13/SCK
  N2: Composant1.MISO, Composant2.D12/MISO
  N3: Composant1.MOSI, Composant2.D11_PWM/MOSI
  N4: Composant1.LCD_CS, Composant2.D10_PWM/SS
  N5: Composant1.LCD_WR_DC, Composant2.D9_PWM
  N6: Composant1.LCD_Y+, Composant2.A2
  N7: Composant1.LCD_X+, Composant2.D7
  N8: Composant1.LCD_Y-, Composant2.D8
  N9: Composant1.LCD_X-, Composant2.A3
  N10: Composant2.D2, Composant2.D6_PWM, PIR1.SIG
  5V: Composant2.5V, PIR1.VDD
  GND: Composant2.GND, PIR1.GND

custom parts:
  Adafruit 2.8inch Resistive TFT: Add some jazz & pizazz to your project with a color touchscreen LCD. This TFT display is big (2.8" diagonal) bright (4 white-LED backlight) and colorful! 240x320 pixels with individual RGB pixel control, this has way more resolution than a black and white 128x64 display. As a bonus, this display has a resistive touchscreen attached to it already, so you can detect finger presses anywhere on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
  WeMos D1 R2: The D1 R2 is a mini wifi board based on the ESP-8266EX.
  Adafruit PN532 NFC RFID Controller Shield: We've taken our popular Adafruit PN532 breakout board and turned it into a shield - the perfect tool for any 13.56MHz RFID or NFC application. The Adafruit NFC shield uses the PN532 chip-set (the most popular NFC chip on the market) and is what is embedded in pretty much every phone or device that does NFC. This chipset is very powerful, and can pretty much do it all, such as read and write to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
